// Logisim project 3 bit multiplication modified.circ as structural Verilog: 4 circuits, main circuit main
module main (
  input  A2,
  input  A1,
  input  A0,
  input  B2,
  input  B1,
  input  B0,
  output P4,
  output P3,
  output P2,
  output P1,
  output P0
);

  wire and_2_out, and_3_out, and_4_out, b2d_converter_1_a, b2d_converter_1_b, b2d_converter_1_c,
       b2d_converter_1_d, b2d_converter_1_e, b2d_converter_1_f, b2d_converter_1_g, half_adder_1_c, or_1_out,
       or_2_out, or_3_out, xor_1_out;

  and and_1 (P0, B0, A0);
  and and_2 (and_2_out, B0, A1);
  and and_3 (and_3_out, B1, A0);
  and and_4 (and_4_out, B1, A1);
  xor xor_1 (xor_1_out, B2, A2);
  Half_Adder half_adder_1 (.X(and_2_out), .Y(and_3_out), .S(P1), .C(half_adder_1_c));
  Half_Adder half_adder_2 (.X(half_adder_1_c), .Y(and_4_out), .S(P2), .C(P3));
  or or_1 (or_1_out, P3, P2);
  or or_2 (or_2_out, P1, P0);
  or or_3 (or_3_out, or_1_out, or_2_out);
  B2D_converter b2d_converter_1 (
    .P3(P0), .P2(P1), .P1(P2), .P0(P3), .a(b2d_converter_1_a), .b(b2d_converter_1_b), .c(b2d_converter_1_c),
    .d(b2d_converter_1_d), .e(b2d_converter_1_e), .f(b2d_converter_1_f), .g(b2d_converter_1_g));
  and and_5 (P4, or_3_out, xor_1_out);
  _7_Segment_Display u_7_segment_display_1 (.g(P4));  // open: f, a, b, e, d, c, dp
  _7_Segment_Display u_7_segment_display_2 (
    .g(b2d_converter_1_g), .f(b2d_converter_1_f), .a(b2d_converter_1_a), .b(b2d_converter_1_b),
    .e(b2d_converter_1_e), .d(b2d_converter_1_d), .c(b2d_converter_1_c));  // open: dp
endmodule

// HA
module Half_Adder (
  input  X,
  input  Y,
  output S,
  output C
);

  xor xor_1 (S, X, Y);
  and and_1 (C, X, Y);
endmodule

module B2D_converter (
  input  P3,
  input  P2,
  input  P1,
  input  P0,
  output a,
  output b,
  output c,
  output d,
  output e,
  output f,
  output g
);

  wire and_1_out, and_2_out, and_3_out, and_4_out, and_5_out, and_6_out, and_7_out, and_8_out, and_9_out,
       and_10_out, and_11_out, and_12_out, and_13_out, and_14_out, and_15_out, and_16_out, and_17_out,
       not_1_out, not_2_out, not_3_out, not_4_out, not_5_out, not_6_out, not_7_out, not_8_out, not_9_out,
       not_10_out, not_11_out, not_12_out, not_13_out, not_14_out, not_15_out, not_16_out, not_17_out,
       not_18_out, not_19_out, not_20_out, not_21_out;

  not not_1 (not_1_out, P1);
  and and_1 (and_1_out, not_1_out, not_2_out);
  not not_2 (not_2_out, P3);
  and and_2 (and_2_out, P1, P3);
  not not_3 (not_3_out, P1);
  not not_4 (not_4_out, P2);
  and and_3 (and_3_out, not_4_out, not_5_out);
  not not_5 (not_5_out, P3);
  and and_4 (and_4_out, P2, P3);
  not not_6 (not_6_out, P2);
  not not_7 (not_7_out, P1);
  and and_5 (and_5_out, not_7_out, not_8_out);
  not not_8 (not_8_out, P3);
  not not_9 (not_9_out, P1);
  and and_6 (and_6_out, not_9_out, P2);
  and and_7 (and_7_out, P2, not_10_out);
  not not_10 (not_10_out, P3);
  not not_11 (not_11_out, P2);
  and and_8 (and_8_out, P1, not_11_out, P3);
  not not_12 (not_12_out, P1);
  and and_9 (and_9_out, not_12_out, not_13_out);
  not not_13 (not_13_out, P3);
  and and_10 (and_10_out, P2, not_14_out);
  not not_14 (not_14_out, P3);
  and and_11 (and_11_out, P0, P1);
  not not_15 (not_15_out, P2);
  and and_12 (and_12_out, not_15_out, not_16_out);
  not not_16 (not_16_out, P3);
  and and_13 (and_13_out, P1, not_17_out);
  not not_17 (not_17_out, P2);
  and and_14 (and_14_out, P1, not_18_out);
  not not_18 (not_18_out, P3);
  not not_19 (not_19_out, P1);
  and and_15 (and_15_out, not_19_out, P2);
  and and_16 (and_16_out, P1, not_20_out);
  not not_20 (not_20_out, P2);
  and and_17 (and_17_out, P1, not_21_out);
  not not_21 (not_21_out, P3);
  or or_1 (a, and_1_out, P2, and_2_out, P0);
  or or_2 (b, not_3_out, and_3_out, and_4_out, P0);
  or or_3 (c, not_6_out, P3, P1, P0);
  or or_4 (d, and_5_out, and_6_out, and_7_out, and_8_out, P0);
  or or_5 (e, and_9_out, and_10_out, and_11_out);
  or or_6 (f, and_12_out, and_13_out, and_14_out, P0);
  or or_7 (g, and_15_out, and_16_out, and_17_out, P0);
endmodule

module sign_display (
  input  P4,
  output a,
  output b,
  output c,
  output d,
  output e,
  output f,
  output g
);


  assign a = 1'b0;
  assign b = 1'b0;
  assign c = 1'b0;
  assign d = 1'b0;
  assign e = 1'b0;
  assign f = 1'b0;
  assign g = P4;
endmodule
