// Logisim project ALU 1st Trial Version.circ as structural Verilog: 2 circuits, main circuit main
module main (
  input  As,
  input  A1,
  input  A0,
  input  Bs,
  input  B1,
  input  B0,
  input  in_7,
  input  in_8
);

  wire adder_subtractor_p9, adder_subtractor_p10, adder_subtractor_p11, adder_subtractor_p12,
       adder_subtractor_p13, b2d_converter_1_a, b2d_converter_1_b, b2d_converter_1_c, b2d_converter_1_d,
       b2d_converter_1_e, b2d_converter_1_f, b2d_converter_1_g, multiplexer_1_out, multiplexer_2_out,
       multiplexer_3_out, multiplexer_4_out, multiplexer_5_out, multiplexer_6_out, multiplexer_7_out,
       Multiplier_p0, Multiplier_p1, Multiplier_p2, Multiplier_p3, Multiplier_p4, remainder_div_by_0,
       remainder_r0, remainder_r1, remainder_sign, remainder_zero;

  // adder_and_subtractor_3_bit_modified___2__main adder_subtractor: pin names not known; wires that end beside it: A0, A0, A1, B0, B1, A1, Bs, in_7, adder_subtractor_p9, adder_subtractor_p10, adder_subtractor_p11, adder_subtractor_p12, adder_subtractor_p13
  Multi Multiplier (
    .A2(A1), .A1(A1), .A0(A0), .B2(Bs), .B1(B1), .B0(B0), .P4(Multiplier_p4), .P3(Multiplier_p3),
    .P2(Multiplier_p2), .P1(Multiplier_p1), .P0(Multiplier_p0));
  Remainder_ALU_main remainder (
    .AS(A1), .A1(A1), .A0(A0), .BS(Bs), .B1(B1), .B0(B0), .R0(remainder_r0), .R1(remainder_r1),
    .div_by_0(remainder_div_by_0), .Zero(remainder_zero), .Sign(remainder_sign));
  Multiplexer #(.select(2)) multiplexer_1 (
    .in0(1'b0), .in1(1'b0), .in2(1'b0), .in3(remainder_div_by_0), .out(multiplexer_1_out), .sel({in_8, in_7}));  // open: en
  Multiplexer #(.select(2)) multiplexer_2 (
    .in0(adder_subtractor_p9), .in1(adder_subtractor_p9), .in2(1'b0), .in3(remainder_zero),
    .out(multiplexer_2_out), .sel({in_8, in_7}));  // open: en
  Multiplexer #(.select(2)) multiplexer_3 (
    .in0(adder_subtractor_p13), .in1(adder_subtractor_p13), .in2(Multiplier_p4), .in3(remainder_sign),
    .out(multiplexer_3_out), .sel({in_8, in_7}));  // open: en
  Multiplexer #(.select(2)) multiplexer_4 (
    .in0(adder_subtractor_p10), .in1(adder_subtractor_p10), .in2(Multiplier_p0), .in3(remainder_r0),
    .out(multiplexer_4_out), .sel({in_8, in_7}));  // open: en
  Multiplexer #(.select(2)) multiplexer_5 (
    .in0(adder_subtractor_p11), .in1(adder_subtractor_p11), .in2(Multiplier_p1), .in3(remainder_r1),
    .out(multiplexer_5_out), .sel({in_8, in_7}));  // open: en
  Multiplexer #(.select(2)) multiplexer_6 (
    .in0(adder_subtractor_p12), .in1(adder_subtractor_p12), .in2(Multiplier_p2), .in3(1'b0),
    .out(multiplexer_6_out), .sel({in_8, in_7}));  // open: en
  Multiplexer #(.select(2)) multiplexer_7 (
    .in0(1'b0), .in1(1'b0), .in2(Multiplier_p3), .in3(1'b0), .out(multiplexer_7_out), .sel({in_8, in_7}));  // open: en
  LED Div_By_Zero (.in(multiplexer_1_out));
  LED Zero_Flag (.in(multiplexer_2_out));
  LED Sign (.in(multiplexer_3_out));
  B2D_converter b2d_converter_1 (
    .P3(multiplexer_4_out), .P2(multiplexer_5_out), .P1(multiplexer_6_out), .P0(multiplexer_7_out),
    .a(b2d_converter_1_a), .b(b2d_converter_1_b), .c(b2d_converter_1_c), .d(b2d_converter_1_d),
    .e(b2d_converter_1_e), .f(b2d_converter_1_f), .g(b2d_converter_1_g));
  _7_Segment_Display u_7_segment_display_1 (
    .g(b2d_converter_1_g), .f(b2d_converter_1_f), .a(b2d_converter_1_a), .b(b2d_converter_1_b),
    .e(b2d_converter_1_e), .d(b2d_converter_1_d), .c(b2d_converter_1_c));  // open: dp
  _7_Segment_Display u_7_segment_display_2 (.g(multiplexer_3_out));  // open: f, a, b, e, d, c, dp

  assign As = A1;
endmodule

module Multi (
  input  A2,
  input  A1,
  input  A0,
  input  B2,
  input  B1,
  input  B0,
  output P4,
  output P3,
  output P2,
  output P1,
  output P0
);

  wire and_2_out, and_3_out, and_4_out, half_adder_1_c, or_1_out, or_2_out, or_3_out;

  and and_1 (P0, B0, A0);
  and and_2 (and_2_out, B0, A1);
  and and_3 (and_3_out, B1, A0);
  and and_4 (and_4_out, B1, A1);
  xor xor_1 (P4, B2, A2);
  Half_Adder half_adder_1 (.X(and_2_out), .Y(and_3_out), .S(P1), .C(half_adder_1_c));
  Half_Adder half_adder_2 (.X(half_adder_1_c), .Y(and_4_out), .S(P2), .C(P3));
  or or_1 (or_1_out, P3, P2);
  or or_2 (or_2_out, P1, P0);
  or or_3 (or_3_out, or_1_out, or_2_out);
endmodule
