// Logisim project Remainder ALU.circ as structural Verilog: 3 circuits, main circuit main
module main (
  input  AS,
  input  A1,
  input  A0,
  input  BS,
  input  B1,
  input  B0,
  output R0,
  output R1,
  output div_by_0,
  output Zero,
  output Sign
);

  wire and_1_out, and_4_out, n7_segment_1_a, n7_segment_1_b, n7_segment_1_c_2, n7_segment_1_d_2,
       n7_segment_1_e, n7_segment_1_f, n7_segment_1_g, nand_1_out, nor_3_out, not_1_out;

  not not_1 (not_1_out, A0);
  and and_1 (and_1_out, A0, B1);
  nand nand_1 (nand_1_out, A1, B0);
  and and_2 (R1, A1, not_1_out, B1, B0);
  nor nor_1 (div_by_0, B1, B0);
  and and_3 (R0, and_1_out, nand_1_out);
  nor nor_2 (Zero, R0, div_by_0, R1);
  nor nor_3 (nor_3_out, Zero, div_by_0);
  _7_segment u_7_segment_1 (
    .D(R1), .C(R0), .a(n7_segment_1_a), .b(n7_segment_1_b), .c_2(n7_segment_1_c_2), .d_2(n7_segment_1_d_2),
    .e(n7_segment_1_e), .f(n7_segment_1_f), .g(n7_segment_1_g));
  _7_Segment_Display u_7_segment_display_1 (.g(and_4_out));  // open: f, a, b, e, d, c, dp
  and and_4 (and_4_out, nor_3_out, AS);
  _7_Segment_Display u_7_segment_display_2 (
    .g(n7_segment_1_g), .f(n7_segment_1_f), .a(n7_segment_1_a), .b(n7_segment_1_b), .e(n7_segment_1_e),
    .d(n7_segment_1_d_2), .c(n7_segment_1_c_2));  // open: dp

  assign Sign = AS;
endmodule

module Full_Adder (
  input  A,
  input  B,
  input  Cin,
  output S,
  output Co
);

  wire and_1_out, and_2_out, xor_1_out;

  xor xor_1 (xor_1_out, A, B);
  xor xor_2 (S, xor_1_out, Cin);
  and and_1 (and_1_out, xor_1_out, Cin);
  and and_2 (and_2_out, A, B);
  or or_1 (Co, and_1_out, and_2_out);
endmodule

module _7_segment (
  input  D,
  input  C,
  output a,
  output b,
  output c_2,
  output d_2,
  output e,
  output f,
  output g
);

  wire not_1_out, not_2_out, not_3_out, not_5_out, not_6_out;

  not not_1 (not_1_out, C);
  not not_2 (not_2_out, D);
  not not_3 (not_3_out, C);
  not not_4 (e, C);
  not not_5 (not_5_out, D);
  not not_6 (not_6_out, C);
  or or_1 (a, not_1_out, D);
  or or_2 (c_2, not_2_out, C);
  or or_3 (d_2, not_3_out, D);
  and and_1 (f, not_5_out, not_6_out);

  assign b = 1'b1;
  assign g = D;
endmodule
