// Logisim project adder and subtractor 3 bit modified .circ as structural Verilog: 5 circuits, main circuit main
module main (
  input  B1,
  input  B0,
  input  A0,
  input  A1,
  input  A_sign,
  input  B_sign,
  input  Cin,
  output out_8,
  output Sign,
  output C_out,
  output Out1,
  output Out0,
  output out_13
);

  wire and_1_out, and_3_out, and_4_out, and_5_out, binary_to_decimal_1_a_2, binary_to_decimal_1_b_2,
       binary_to_decimal_1_c_2, binary_to_decimal_1_d_2, binary_to_decimal_1_e, binary_to_decimal_1_f,
       binary_to_decimal_1_g, full_adder_1_out_4, full_adder_1_out_5, full_adder_2_out_4, full_adder_2_out_5,
       n2_s_complement_1_out_3, n2_s_complement_1_out_4, nor_1_out, not_1_out, not_2_out, not_3_out,
       not_4_out, not_5_out, xor_1_out, xor_2_out, xor_3_out, xor_4_out, xor_5_out, xor_6_out;

  or or_1 (Sign, and_5_out, and_1_out);
  xor xor_1 (xor_1_out, B1, and_4_out);
  not not_1 (not_1_out, full_adder_1_out_5);
  and and_1 (and_1_out, not_1_out, xor_5_out);
  and and_2 (C_out, full_adder_1_out_5, not_2_out);
  xor xor_2 (xor_2_out, A0, and_3_out);
  not not_2 (not_2_out, xor_5_out);
  Multiplexer #(.enable("false")) multiplexer_1 (
    .in0(full_adder_1_out_4), .in1(n2_s_complement_1_out_3), .out(Out1), .sel(and_1_out));
  full_adder full_adder_1 (
    .in_1(full_adder_2_out_5), .in_2(xor_2_out), .in_3(xor_1_out), .out_4(full_adder_1_out_4),
    .out_5(full_adder_1_out_5));
  xor xor_3 (xor_3_out, B0, and_4_out);
  _2_s_Complement u_2_s_complement_1 (
    .in_1(full_adder_1_out_4), .in_2(full_adder_2_out_4), .out_3(n2_s_complement_1_out_3),
    .out_4(n2_s_complement_1_out_4));
  xor xor_4 (xor_4_out, A1, and_3_out);
  full_adder full_adder_2 (
    .in_1(xor_5_out), .in_2(xor_4_out), .in_3(xor_3_out), .out_4(full_adder_2_out_4),
    .out_5(full_adder_2_out_5));
  Multiplexer #(.enable("false")) multiplexer_2 (
    .in0(full_adder_2_out_4), .in1(n2_s_complement_1_out_4), .out(Out0), .sel(and_1_out));
  and and_3 (and_3_out, A_sign, not_3_out);
  and and_4 (and_4_out, not_4_out, xor_6_out);
  not not_3 (not_3_out, xor_6_out);
  not not_4 (not_4_out, A_sign);
  xor xor_5 (xor_5_out, A_sign, xor_6_out);
  Binary_to_Decimal binary_to_decimal_1 (
    .A(1'b0), .B(C_out), .C(Out1), .D(Out0), .a_2(binary_to_decimal_1_a_2), .b_2(binary_to_decimal_1_b_2),
    .c_2(binary_to_decimal_1_c_2), .d_2(binary_to_decimal_1_d_2), .e(binary_to_decimal_1_e),
    .f(binary_to_decimal_1_f), .g(binary_to_decimal_1_g));
  xor xor_6 (xor_6_out, B_sign, Cin);
  and and_5 (and_5_out, A_sign, xor_6_out);
  _7_Segment_Display u_7_segment_display_1 (.g(Sign));  // open: f, a, b, e, d, c, dp
  nor nor_1 (nor_1_out, Out0, Out1);
  not not_5 (not_5_out, C_out);
  _7_Segment_Display u_7_segment_display_2 (
    .g(binary_to_decimal_1_g), .f(binary_to_decimal_1_f), .a(binary_to_decimal_1_a_2),
    .b(binary_to_decimal_1_b_2), .e(binary_to_decimal_1_e), .d(binary_to_decimal_1_d_2),
    .c(binary_to_decimal_1_c_2));  // open: dp
  and and_6 (out_13, nor_1_out, not_5_out);
endmodule

module full_adder (
  input  in_1,
  input  in_2,
  input  in_3,
  output out_4,
  output out_5
);

  wire half_adder_1_out_3, half_adder_1_out_4, half_adder_2_out_4;

  half_adder half_adder_1 (.in_1(in_2), .in_2(in_3), .out_3(half_adder_1_out_3), .out_4(half_adder_1_out_4));
  half_adder half_adder_2 (.in_1(in_1), .in_2(half_adder_1_out_3), .out_3(out_4), .out_4(half_adder_2_out_4));
  or or_1 (out_5, half_adder_2_out_4, half_adder_1_out_4);
endmodule

module half_adder (
  input  in_1,
  input  in_2,
  output out_3,
  output out_4
);

  xor xor_1 (out_3, in_1, in_2);
  and and_1 (out_4, in_1, in_2);
endmodule

// 2's
module _2_s_Complement (
  input  in_1,
  input  in_2,
  output out_3,
  output out_4
);

  xor xor_1 (out_3, in_1, in_2);

  assign out_4 = in_2;
endmodule

// B to D
module Binary_to_Decimal (
  input  A,
  input  B,
  input  C,
  input  D,
  output a_2,
  output b_2,
  output c_2,
  output d_2,
  output e,
  output f,
  output g
);

  wire and_1_out, and_2_out, and_3_out, and_4_out, and_5_out, and_6_out, and_7_out, and_8_out, and_9_out,
       and_10_out, and_11_out, and_12_out, and_13_out, and_14_out, and_15_out, and_16_out, not_1_out,
       not_2_out, not_3_out, not_4_out, not_5_out, not_6_out, not_7_out, not_8_out, not_9_out, not_10_out,
       not_11_out, not_12_out, not_13_out, not_14_out, not_15_out, not_16_out, not_17_out, not_18_out,
       not_19_out, not_20_out, not_21_out;

  not not_1 (not_1_out, B);
  and and_1 (and_1_out, not_1_out, not_2_out);
  not not_2 (not_2_out, D);
  and and_2 (and_2_out, B, D);
  not not_3 (not_3_out, B);
  not not_4 (not_4_out, C);
  and and_3 (and_3_out, not_4_out, not_5_out);
  not not_5 (not_5_out, D);
  and and_4 (and_4_out, C, D);
  not not_6 (not_6_out, C);
  or or_1 (c_2, not_6_out, D, B);
  not not_7 (not_7_out, B);
  and and_5 (and_5_out, not_7_out, not_8_out);
  not not_8 (not_8_out, D);
  not not_9 (not_9_out, B);
  and and_6 (and_6_out, not_9_out, C);
  and and_7 (and_7_out, C, not_10_out);
  not not_10 (not_10_out, D);
  and and_8 (and_8_out, B, not_11_out, D);
  not not_11 (not_11_out, C);
  not not_12 (not_12_out, B);
  and and_9 (and_9_out, not_12_out, not_13_out);
  not not_13 (not_13_out, D);
  and and_10 (and_10_out, C, not_14_out);
  not not_14 (not_14_out, D);
  not not_15 (not_15_out, C);
  and and_11 (and_11_out, not_15_out, not_16_out);
  not not_16 (not_16_out, D);
  and and_12 (and_12_out, B, not_17_out);
  not not_17 (not_17_out, C);
  and and_13 (and_13_out, B, not_18_out);
  not not_18 (not_18_out, D);
  not not_19 (not_19_out, B);
  and and_14 (and_14_out, not_19_out, C);
  and and_15 (and_15_out, B, not_20_out);
  not not_20 (not_20_out, C);
  and and_16 (and_16_out, B, not_21_out);
  not not_21 (not_21_out, D);
  or or_2 (a_2, and_1_out, C, and_2_out, A);
  or or_3 (b_2, not_3_out, and_3_out, and_4_out);
  or or_4 (d_2, and_5_out, and_6_out, and_7_out, and_8_out, A);
  or or_5 (e, and_9_out, and_10_out);
  or or_6 (f, and_11_out, and_12_out, and_13_out, A);
  or or_7 (g, and_14_out, and_15_out, and_16_out, A);
endmodule
