// Logisim project adder and subtractor 3 bit.circ as structural Verilog: 5 circuits, main circuit main
module main (
  input  [1:0] B,
  input  [1:0] A,
  input  A_sign,
  input  B_sign,
  input  in_5,
  output out_6,
  output out_7,
  output out_8,
  output out_9
);

  wire and_1_out, and_3_out, and_4_out, and_5_out, full_adder_1_out_4, full_adder_1_out_5,
       full_adder_2_out_4, full_adder_2_out_5, n2_s_complement_1_out_3, n2_s_complement_1_out_4, not_1_out,
       not_2_out, not_3_out, not_4_out, or_2_out, xor_1_out, xor_2_out, xor_3_out, xor_4_out, xor_5_out,
       xor_6_out;

  or or_1 (out_6, and_5_out, and_1_out);
  xor xor_1 (xor_1_out, B[1], and_4_out);
  not not_1 (not_1_out, full_adder_1_out_5);
  and and_1 (and_1_out, not_1_out, xor_5_out);
  and and_2 (out_7, full_adder_1_out_5, not_2_out);
  xor xor_2 (xor_2_out, A[1], and_3_out);
  not not_2 (not_2_out, xor_5_out);
  Multiplexer #(.enable("false")) multiplexer_1 (
    .in0(full_adder_1_out_4), .in1(n2_s_complement_1_out_3), .out(out_8), .sel(and_1_out));
  full_adder full_adder_1 (
    .in_1(full_adder_2_out_5), .in_2(xor_2_out), .in_3(xor_1_out), .out_4(full_adder_1_out_4),
    .out_5(full_adder_1_out_5));
  xor xor_3 (xor_3_out, B[0], and_4_out);
  _2_s_Complement u_2_s_complement_1 (
    .in_1(full_adder_1_out_4), .in_2(full_adder_2_out_4), .out_3(n2_s_complement_1_out_3),
    .out_4(n2_s_complement_1_out_4));
  xor xor_4 (xor_4_out, A[0], and_3_out);
  full_adder full_adder_2 (
    .in_1(or_2_out), .in_2(xor_4_out), .in_3(xor_3_out), .out_4(full_adder_2_out_4),
    .out_5(full_adder_2_out_5));
  Multiplexer #(.enable("false")) multiplexer_2 (
    .in0(full_adder_2_out_4), .in1(n2_s_complement_1_out_4), .out(out_9), .sel(and_1_out));
  or or_2 (or_2_out, and_3_out, and_4_out);
  and and_3 (and_3_out, A_sign, not_3_out);
  and and_4 (and_4_out, not_4_out, xor_6_out);
  not not_3 (not_3_out, xor_6_out);
  not not_4 (not_4_out, A_sign);
  xor xor_5 (xor_5_out, A_sign, xor_6_out);
  xor xor_6 (xor_6_out, B_sign, in_5);
  and and_5 (and_5_out, A_sign, xor_6_out);
endmodule

module \input  (
  input  A_sign,
  input  [1:0] A,
  input  [1:0] B,
  input  B_sign,
  input  operation_code,
  input  in_6,
  output out_7,
  output out_8,
  output out_9,
  output out_10
);

  wire and_1_out, and_3_out, and_4_out, and_5_out, and_6_out, full_adder_1_out_4, full_adder_1_out_5,
       full_adder_2_out_4, full_adder_2_out_5, n2_s_complement_1_out_3, n2_s_complement_1_out_4, not_1_out,
       not_2_out, not_3_out, not_4_out, not_5_out, or_2_out, xor_1_out, xor_2_out, xor_3_out, xor_4_out,
       xor_5_out, xor_6_out;

  xor xor_1 (xor_1_out, A[1], and_3_out);
  not not_1 (not_1_out, full_adder_1_out_5);
  and and_1 (and_1_out, not_1_out, xor_6_out);
  or or_1 (out_7, and_1_out, and_6_out);
  not not_2 (not_2_out, xor_6_out);
  and and_2 (out_8, full_adder_1_out_5, not_2_out);
  xor xor_2 (xor_2_out, B[1], and_4_out);
  full_adder full_adder_1 (
    .in_1(full_adder_2_out_5), .in_2(xor_2_out), .in_3(xor_1_out), .out_4(full_adder_1_out_4),
    .out_5(full_adder_1_out_5));
  Multiplexer #(.enable("false")) multiplexer_1 (
    .in0(full_adder_1_out_4), .in1(n2_s_complement_1_out_3), .out(out_9), .sel(and_1_out));
  xor xor_3 (xor_3_out, A[0], and_3_out);
  _2_s_Complement u_2_s_complement_1 (
    .in_1(full_adder_1_out_4), .in_2(full_adder_2_out_4), .out_3(n2_s_complement_1_out_3),
    .out_4(n2_s_complement_1_out_4));
  xor xor_4 (xor_4_out, B[0], and_4_out);
  or or_2 (or_2_out, and_3_out, and_4_out);
  full_adder full_adder_2 (
    .in_1(or_2_out), .in_2(xor_4_out), .in_3(xor_3_out), .out_4(full_adder_2_out_4),
    .out_5(full_adder_2_out_5));
  Multiplexer #(.enable("false")) multiplexer_2 (
    .in0(full_adder_2_out_4), .in1(n2_s_complement_1_out_4), .out(out_10), .sel(and_1_out));
  and and_3 (and_3_out, A_sign, not_3_out);
  and and_4 (and_4_out, not_4_out, xor_5_out);
  not not_3 (not_3_out, xor_5_out);
  not not_4 (not_4_out, A_sign);
  xor xor_5 (xor_5_out, B_sign, and_5_out);
  xor xor_6 (xor_6_out, A_sign, xor_5_out);
  and and_5 (and_5_out, not_5_out, in_6);
  not not_5 (not_5_out, operation_code);
  and and_6 (and_6_out, A_sign, xor_6_out);

  // Notes on the sheet:
  //   A sign
  //   B sign
endmodule

module full_adder (
  input  in_1,
  input  in_2,
  input  in_3,
  output out_4,
  output out_5
);

  wire half_adder_1_out_3, half_adder_1_out_4, half_adder_2_out_4;

  half_adder half_adder_1 (.in_1(in_2), .in_2(in_3), .out_3(half_adder_1_out_3), .out_4(half_adder_1_out_4));
  half_adder half_adder_2 (.in_1(in_1), .in_2(half_adder_1_out_3), .out_3(out_4), .out_4(half_adder_2_out_4));
  or or_1 (out_5, half_adder_2_out_4, half_adder_1_out_4);
endmodule

module half_adder (
  input  in_1,
  input  in_2,
  output out_3,
  output out_4
);

  xor xor_1 (out_3, in_1, in_2);
  and and_1 (out_4, in_1, in_2);
endmodule

module _2_s_Complement (
  input  in_1,
  input  in_2,
  output out_3,
  output out_4
);

  xor xor_1 (out_3, in_1, in_2);

  assign out_4 = in_2;
endmodule
